// Logisim project Processor.circ as structural Verilog: 32 circuits, main circuit SR_FF
module SR_FF (
  input  in_1,
  input  in_2,
  input  in_3,
  output out_4,
  output out_5
);

  wire nand_1_out, nand_2_out;

  nand nand_1 (nand_1_out, in_1, in_2);
  nand nand_2 (nand_2_out, in_2, in_3);
  nand nand_3 (out_4, nand_1_out, out_5);
  nand nand_4 (out_5, out_4, nand_2_out);
endmodule

module D_FF_level_triggered (
  input  in_1,
  input  CLK,
  output out_3,
  output out_4
);

  wire nand_1_out, nand_2_out, not_1_out;

  not not_1 (not_1_out, in_1);
  nand nand_1 (nand_1_out, in_1, CLK);
  nand nand_2 (nand_2_out, CLK, not_1_out);
  nand nand_3 (out_3, nand_1_out, out_4);
  nand nand_4 (out_4, out_3, nand_2_out);
endmodule

module PIPO_Register (
  input  in_1,
  input  in_2,
  input  in_3,
  input  in_4,
  input  LD,
  output out_6,
  output out_7,
  output out_8,
  output out_9
);

  wire d_ff_edge_triggered_1_out_4, d_ff_edge_triggered_2_out_4, d_ff_edge_triggered_3_out_4,
       d_ff_edge_triggered_4_out_4;

  D_FF_edge_triggered d_ff_edge_triggered_1 (
    .in_1(in_1), .in_2(LD), .out_3(out_6), .out_4(d_ff_edge_triggered_1_out_4));
  LED led_1 (.in(d_ff_edge_triggered_1_out_4));
  D_FF_edge_triggered d_ff_edge_triggered_2 (
    .in_1(in_2), .in_2(LD), .out_3(out_7), .out_4(d_ff_edge_triggered_2_out_4));
  LED led_2 (.in(d_ff_edge_triggered_2_out_4));
  D_FF_edge_triggered d_ff_edge_triggered_3 (
    .in_1(in_3), .in_2(LD), .out_3(out_8), .out_4(d_ff_edge_triggered_3_out_4));
  LED led_3 (.in(d_ff_edge_triggered_3_out_4));
  D_FF_edge_triggered d_ff_edge_triggered_4 (
    .in_1(in_4), .in_2(LD), .out_3(out_9), .out_4(d_ff_edge_triggered_4_out_4));
  LED led_4 (.in(d_ff_edge_triggered_4_out_4));
endmodule

module Register_4bit (
  input  [3:0] in_1,
  input  LD,
  output [3:0] out_3
);

  PIPO_Register pipo_register_1 (
    .in_1(in_1[0]), .in_2(in_1[1]), .in_3(in_1[2]), .in_4(in_1[3]), .LD(LD), .out_6(out_3[0]),
    .out_7(out_3[1]), .out_8(out_3[2]), .out_9(out_3[3]));
endmodule

module Full_Adder (
  input  in_1,
  input  in_2,
  input  Cin,
  output Sum,
  output Cout
);

  wire and_1_out, and_2_out, xor_1_out;

  xor xor_1 (xor_1_out, in_1, in_2);
  and and_1 (and_1_out, xor_1_out, Cin);
  xor xor_2 (Sum, xor_1_out, Cin);
  and and_2 (and_2_out, in_2, in_1);
  or or_1 (Cout, and_1_out, and_2_out);
endmodule

module ALU (
  input  [3:0] Acc,
  input  [3:0] D_Reg,
  input  S0,
  input  S1,
  input  S2,
  input  Ir,
  input  Il,
  output Cout,
  output [3:0] ResultToAcc
);

  wire [3:0] and_1_out, fourbit_adder_subtractor_1_s0, not_1_out, or_1_out, shift_unit_1_s0, xor_1_out;

  assign not_1_out = ~Acc;  // NOT_Gate not_1, 4 bits wide
  assign and_1_out = Acc & D_Reg;  // AND_Gate and_1, 4 bits wide
  assign or_1_out = Acc | D_Reg;  // OR_Gate or_1, 4 bits wide
  assign xor_1_out = Acc ^ D_Reg;  // XOR_Gate xor_1, 4 bits wide
  FourBit_Adder_Subtractor fourbit_adder_subtractor_1 (
    .A0(Acc[0]), .A1(Acc[1]), .A2(Acc[2]), .A3(Acc[3]), .B0(D_Reg[0]), .B1(D_Reg[1]), .B2(D_Reg[2]),
    .B3(D_Reg[3]), .sub_mode(S2), .S0(fourbit_adder_subtractor_1_s0[0]),
    .S1(fourbit_adder_subtractor_1_s0[1]), .S2(fourbit_adder_subtractor_1_s0[2]),
    .S3(fourbit_adder_subtractor_1_s0[3]), .Cout(Cout));
  Shift_Unit shift_unit_1 (
    .Ir(Ir), .A0(Acc[0]), .A1(Acc[1]), .A2(Acc[2]), .A3(Acc[3]), .Il(Il), .right_shift(S2),
    .S0(shift_unit_1_s0[0]), .S1(shift_unit_1_s0[1]), .S2(shift_unit_1_s0[2]), .S3(shift_unit_1_s0[3]));
  Multiplexer #(.select(3), .width(4)) multiplexer_1 (
    .in0(fourbit_adder_subtractor_1_s0), .in1(fourbit_adder_subtractor_1_s0), .in2(not_1_out),
    .in3(and_1_out), .in4(or_1_out), .in5(xor_1_out), .in6(shift_unit_1_s0), .in7(shift_unit_1_s0),
    .out(ResultToAcc), .sel({S2, S1, S0}));
endmodule

module FourBit_Adder_Subtractor (
  input  A0,
  input  A1,
  input  A2,
  input  A3,
  input  B0,
  input  B1,
  input  B2,
  input  B3,
  input  sub_mode,
  output S0,
  output S1,
  output S2,
  output S3,
  output Cout
);

  wire full_adder_1_cout, full_adder_2_cout, full_adder_3_cout, xor_1_out, xor_2_out, xor_3_out, xor_4_out;

  xor xor_1 (xor_1_out, sub_mode, B0);
  xor xor_2 (xor_2_out, sub_mode, B1);
  xor xor_3 (xor_3_out, sub_mode, B2);
  xor xor_4 (xor_4_out, sub_mode, B3);
  Full_Adder full_adder_1 (.in_1(A0), .in_2(xor_1_out), .Cin(sub_mode), .Sum(S0), .Cout(full_adder_1_cout));
  Full_Adder full_adder_2 (.in_1(A1), .in_2(xor_2_out), .Cin(full_adder_1_cout), .Sum(S1), .Cout(full_adder_2_cout));
  Full_Adder full_adder_3 (.in_1(A2), .in_2(xor_3_out), .Cin(full_adder_2_cout), .Sum(S2), .Cout(full_adder_3_cout));
  Full_Adder full_adder_4 (.in_1(A3), .in_2(xor_4_out), .Cin(full_adder_3_cout), .Sum(S3), .Cout(Cout));
endmodule

module D_FF_edge_triggered (
  input  in_1,
  input  in_2,
  output out_3,
  output out_4
);

  D_Flip_Flop d_ff_1 (.D(in_1), .clk(in_2), .Q(out_3), .Qn(out_4));  // open: preset, reset
endmodule

module Shift_Unit (
  input  Ir,
  input  A0,
  input  A1,
  input  A2,
  input  A3,
  input  Il,
  input  right_shift,
  output S0,
  output S1,
  output S2,
  output S3
);

  Multiplexer multiplexer_1 (.in0(Ir), .in1(A1), .out(S0), .sel(right_shift));
  Multiplexer multiplexer_2 (.in0(A0), .in1(A2), .out(S1), .sel(right_shift));
  Multiplexer multiplexer_3 (.in0(A1), .in1(A3), .out(S2), .sel(right_shift));
  Multiplexer multiplexer_4 (.in0(A2), .in1(Il), .out(S3), .sel(right_shift));
endmodule

module Reg_Memory (
);

  RAM ram_1 ();  // open: addr, we, oe, clk, din, dout
  Register_4bit register_4bit_1 ();  // open: in_1, LD, out_3
  Register_4bit register_4bit_2 ();  // open: in_1, LD, out_3
  Register_4bit register_4bit_3 ();  // open: in_1, LD, out_3
  Register_4bit register_4bit_4 ();  // open: in_1, LD, out_3
  Register_4bit register_4bit_5 ();  // open: in_1, LD, out_3
endmodule

module SyncCounter (
  input  EN,
  input  CLK,
  input  RST,
  output out_4,
  output out_5,
  output out_6,
  output out_7
);

  wire and_1_out, and_2_out;

  J_K_Flip_Flop j_k_ff_1 (.J(EN), .K(EN), .clk(CLK), .Q(out_4), .reset(RST));  // open: Qn, preset
  J_K_Flip_Flop j_k_ff_2 (.J(out_4), .K(out_4), .clk(CLK), .Q(out_5), .reset(RST));  // open: Qn, preset
  and and_1 (and_1_out, out_4, out_5);
  J_K_Flip_Flop j_k_ff_3 (.J(and_1_out), .K(and_1_out), .clk(CLK), .Q(out_6), .reset(RST));  // open: Qn, preset
  and and_2 (and_2_out, and_1_out, out_6);
  J_K_Flip_Flop j_k_ff_4 (.J(and_2_out), .K(and_2_out), .clk(CLK), .Q(out_7), .reset(RST));  // open: Qn, preset
endmodule

module ControlUnit (
  input  [3:0] ALU,
  input  [7:0] ADD,
  input  EN,
  input  RST,
  input  CLK,
  input  [3:0] IR,
  output PC_LD,
  output Z_Flag,
  output ALU_EN,
  output PC_EN,
  output MEM_READ,
  output [7:0] out_12,
  output MEM_WRITE,
  output IR_LD,
  output AL_LD,
  output [3:0] T,
  output AH_LD,
  output ACC_SELECT,
  output ACC_LD,
  output MEM_SELECT,
  output PC_CLK,
  output T_RST,
  output MOV_SWITCH,
  output Output_LD
);

  wire and_1_out, nor_1_out, nor_2_out, not_1_out, or_1_out, or_2_out, or_3_out;
  wire [15:0] decoder_1_out0, decoder_2_out0;

  or or_1 (or_1_out, RST, and_1_out);
  or or_2 (or_2_out, RST, T_RST);
  nor nor_1 (nor_1_out, ALU[0], ALU[1], ALU[2], ALU[3]);
  PC pc_1 (
    .EN(EN), .CLK(PC_CLK), .RST(or_1_out), .LD(PC_LD), .D0(ADD[0]), .D1(ADD[1]), .D2(ADD[2]), .D3(ADD[3]),
    .D4(ADD[4]), .D5(ADD[5]), .D6(ADD[6]), .D7(ADD[7]), .out_13(out_12[0]), .out_14(out_12[1]),
    .out_15(out_12[2]), .out_16(out_12[3]), .out_17(out_12[4]), .out_18(out_12[5]), .out_19(out_12[6]),
    .out_20(out_12[7]));
  SyncCounter synccounter_1 (
    .EN(EN), .CLK(CLK), .RST(or_2_out), .out_4(T[0]), .out_5(T[1]), .out_6(T[2]), .out_7(T[3]));
  Decoder #(.select(4)) decoder_1 (
    .out0(decoder_1_out0[0]), .out1(decoder_1_out0[1]), .out2(decoder_1_out0[2]), .out3(decoder_1_out0[3]),
    .out4(decoder_1_out0[4]), .out5(decoder_1_out0[5]), .out6(decoder_1_out0[6]), .out7(decoder_1_out0[7]),
    .out8(decoder_1_out0[8]), .out9(decoder_1_out0[9]), .out10(decoder_1_out0[10]),
    .out11(decoder_1_out0[11]), .out12(decoder_1_out0[12]), .out13(decoder_1_out0[13]),
    .out14(decoder_1_out0[14]), .out15(decoder_1_out0[15]), .sel(IR), .en(nor_2_out));
  and and_1 (and_1_out, decoder_2_out0[7], not_1_out, decoder_1_out0[2]);
  D_Flip_Flop #(.trigger("high")) d_ff_1 (.D(nor_1_out), .clk(ALU_EN), .Q(Z_Flag));  // open: Qn, preset, reset
  not not_1 (not_1_out, Z_Flag);
  Decoder #(.select(4)) decoder_2 (
    .out0(decoder_2_out0[0]), .out1(decoder_2_out0[1]), .out2(decoder_2_out0[2]), .out3(decoder_2_out0[3]),
    .out4(decoder_2_out0[4]), .out5(decoder_2_out0[5]), .out6(decoder_2_out0[6]), .out7(decoder_2_out0[7]),
    .out8(decoder_2_out0[8]), .out9(decoder_2_out0[9]), .out10(decoder_2_out0[10]),
    .out11(decoder_2_out0[11]), .out12(decoder_2_out0[12]), .out13(decoder_2_out0[13]),
    .out14(decoder_2_out0[14]), .out15(decoder_2_out0[15]), .sel(T), .en(EN));
  buf or_3 (or_3_out, decoder_2_out0[6]);  // OR_Gate
  nor nor_2 (nor_2_out, decoder_2_out0[1], decoder_2_out0[0]);
  and and_2 (MOV_SWITCH, or_3_out, decoder_1_out0[0]);
  and and_3 (Output_LD, decoder_2_out0[2], decoder_1_out0[4]);
  PC_LD_SignalGen pc_ld_signalgen_1 (.T(decoder_2_out0), .Z_Flag(Z_Flag), .OP(decoder_1_out0), .PC_LD(PC_LD));
  ALU_EN_SignalGen alu_en_signalgen_1 (.T(decoder_2_out0), .OP(decoder_1_out0), .ALU_EN(ALU_EN));
  PC_EN_SignalGen pc_en_signalgen_1 (.T(decoder_2_out0), .OP(decoder_1_out0), .PC_EN(PC_EN));
  MEM_READ_SignalGen mem_read_signalgen_1 (.T(decoder_2_out0), .OP(decoder_1_out0), .MEM_READ(MEM_READ));
  MEM_WRITE_SignalGen mem_write_signalgen_1 (.T(decoder_2_out0), .OP(decoder_1_out0), .MEM_WRITE(MEM_WRITE));
  IR_LD_SignalGen ir_ld_signalgen_1 (.T(decoder_2_out0), .OP(decoder_1_out0), .IR_LD(IR_LD));
  AL_LD_SignalGen al_ld_signalgen_1 (.T(decoder_2_out0), .OP(decoder_1_out0), .AL_LD(AL_LD));
  AH_LD_SignalGen ah_ld_signalgen_1 (.T(decoder_2_out0), .OP(decoder_1_out0), .AH_LD(AH_LD));
  ACC_SELECT_SignalGen acc_select_signalgen_1 (.T(decoder_2_out0), .OP(decoder_1_out0), .ACC_SELECT(ACC_SELECT));
  ACC_LD_SignalGen acc_ld_signalgen_1 (.T(decoder_2_out0), .OP(decoder_1_out0), .ACC_LD(ACC_LD));
  MEM_SELECT_SignalGen mem_select_signalgen_1 (.T(decoder_2_out0), .OP(decoder_1_out0), .MEM_SELECT(MEM_SELECT));
  PC_CLK_SignalGen pc_clk_signalgen_1 (.T(decoder_2_out0), .OP(decoder_1_out0), .PC_CLK(PC_CLK));
  T_RST_SignalGen t_rst_signalgen_1 (.T(decoder_2_out0), .OP(decoder_1_out0), .T_RST(T_RST));
endmodule

module System_Bus (
  input  [3:0] IR,
  input  [3:0] BR,
  input  [3:0] CR,
  input  [3:0] DR,
  input  [3:0] ACC,
  input  [3:0] MEM,
  input  MEM_SELECT,
  input  ACC_SELECT,
  input  MOV_Switch,
  input  L_LD,
  input  [7:0] PC,
  input  H_LD,
  input  PC_EN,
  input  [3:0] ALU_Output,
  input  ALU_OP,
  output [3:0] DataBus,
  output REG1,
  output REG2,
  output REG3,
  output REG4,
  output [7:0] AddressBus
);

  wire or_1_out;
  wire [3:0] H_out_3, L_out_3, multiplexer_2_out, multiplexer_3_out, multiplexer_4_out;

  Register_4bit L (.in_1(DataBus), .LD(L_LD), .out_3(L_out_3));
  Register_4bit H (.in_1(DataBus), .LD(H_LD), .out_3(H_out_3));
  Decoder #(.select(2)) decoder_1 (
    .out0(REG1), .out1(REG2), .out2(REG3), .out3(REG4), .sel(L_out_3[1:0]), .en(MOV_Switch));
  Multiplexer #(.width(8)) multiplexer_1 (.in0({H_out_3, L_out_3}), .in1(PC), .out(AddressBus), .sel(PC_EN));
  Multiplexer #(.select(3), .width(4)) multiplexer_2 (
    .in0(ACC), .in1(BR), .in2(CR), .in3(DR), .in4(IR), .in5(MEM), .out(multiplexer_2_out),
    .sel({1'b0, L_out_3[3:2]}));  // open: in6, in7
  Multiplexer #(.width(4)) multiplexer_3 (.in0(multiplexer_2_out), .in1(MEM), .out(multiplexer_3_out), .sel(or_1_out));
  Multiplexer #(.width(4)) multiplexer_4 (
    .in0(multiplexer_3_out), .in1(ACC), .out(multiplexer_4_out), .sel(ACC_SELECT));
  or or_1 (or_1_out, MEM_SELECT, PC_EN);
  Multiplexer #(.width(4)) multiplexer_5 (.in0(multiplexer_4_out), .in1(ALU_Output), .out(DataBus), .sel(ALU_OP));

  // Notes on the sheet:
  //   PC Address
  //   AL_H
  //   Reg_To
  //   Reg_From
  //   REG Select
  //   REG LD
endmodule

module PadBits (
  input  [3:0] in_1,
  output [7:0] out_2
);


  assign out_2 = {4'b0000, in_1};
endmodule

module Board (
  input  EN
);

  wire clock_1_out, controlunit_1_acc_ld, controlunit_1_acc_select, controlunit_1_ah_ld, controlunit_1_al_ld,
       controlunit_1_alu_en, controlunit_1_ir_ld, controlunit_1_mem_read, controlunit_1_mem_select,
       controlunit_1_mem_write, controlunit_1_mov_switch, controlunit_1_output_ld, controlunit_1_pc_en,
       controlunit_1_t_rst, or_1_out, RST_out, system_bus_1_reg1, system_bus_1_reg2, system_bus_1_reg3,
       system_bus_1_reg4;
  wire [3:0] alu_1_resulttoacc, BR_out_3, controlunit_1_out_12, controlunit_1_out_12_2, controlunit_1_t,
       ir_1_out_4, multiplexer_1_out, ram_1_dout, register_4bit_1_out_3, register_4bit_2_out_3,
       register_4bit_3_out_3, register_4bit_4_out_3, system_bus_1_databus;
  wire [7:0] system_bus_1_addressbus;

  Clock clock_1 (.out(clock_1_out));
  Button #(.press("passive")) button_1 ();  // open: out
  ALU alu_1 (
    .Acc(register_4bit_3_out_3), .D_Reg(register_4bit_2_out_3), .S0(ir_1_out_4[3]), .S1(ir_1_out_4[2]),
    .S2(ir_1_out_4[1]), .Ir(1'b0), .Il(1'b0), .ResultToAcc(alu_1_resulttoacc));  // open: Cout
  Button RST (.out(RST_out));
  Multiplexer #(.width(4)) multiplexer_1 (
    .in0(system_bus_1_databus), .in1(alu_1_resulttoacc), .out(multiplexer_1_out), .sel(controlunit_1_alu_en));
  or or_1 (or_1_out, controlunit_1_acc_ld, system_bus_1_reg4);
  RAM #(.dataWidth(4)) ram_1 (
    .addr(system_bus_1_addressbus), .we(controlunit_1_mem_write), .oe(controlunit_1_mem_read),
    .clk(clock_1_out), .din(system_bus_1_databus), .dout(ram_1_dout));
  ControlUnit controlunit_1 (
    .EN(EN), .RST(RST_out), .CLK(clock_1_out), .IR(ir_1_out_4), .ADD(system_bus_1_addressbus),
    .ALU(alu_1_resulttoacc), .T(controlunit_1_t), .out_12({controlunit_1_out_12_2, controlunit_1_out_12}),
    .PC_EN(controlunit_1_pc_en), .MEM_READ(controlunit_1_mem_read), .ALU_EN(controlunit_1_alu_en),
    .MEM_WRITE(controlunit_1_mem_write), .IR_LD(controlunit_1_ir_ld), .Output_LD(controlunit_1_output_ld),
    .AL_LD(controlunit_1_al_ld), .ACC_LD(controlunit_1_acc_ld), .MEM_SELECT(controlunit_1_mem_select),
    .T_RST(controlunit_1_t_rst), .MOV_SWITCH(controlunit_1_mov_switch), .AH_LD(controlunit_1_ah_ld),
    .ACC_SELECT(controlunit_1_acc_select));  // open: Z_Flag, PC_LD, PC_CLK
  Hex_Digit_Display hex_digit_display_1 (.value(controlunit_1_t));  // open: dp
  IR ir_1 (.in_1(system_bus_1_databus), .LD(controlunit_1_ir_ld), .RST(controlunit_1_t_rst), .out_4(ir_1_out_4));
  Register_4bit BR (.in_1(system_bus_1_databus), .LD(system_bus_1_reg1), .out_3(BR_out_3));
  Register_4bit register_4bit_1 (.in_1(system_bus_1_databus), .LD(system_bus_1_reg2), .out_3(register_4bit_1_out_3));
  Register_4bit register_4bit_2 (.in_1(system_bus_1_databus), .LD(system_bus_1_reg3), .out_3(register_4bit_2_out_3));
  Register_4bit register_4bit_3 (.in_1(multiplexer_1_out), .LD(or_1_out), .out_3(register_4bit_3_out_3));
  Hex_Digit_Display hex_digit_display_2 (.value(ir_1_out_4));  // open: dp
  Hex_Digit_Display hex_digit_display_3 (.value(register_4bit_3_out_3));  // open: dp
  Hex_Digit_Display hex_digit_display_4 (.value(controlunit_1_out_12_2));  // open: dp
  Hex_Digit_Display hex_digit_display_5 (.value(controlunit_1_out_12));  // open: dp
  Hex_Digit_Display hex_digit_display_6 (.value(register_4bit_2_out_3));  // open: dp
  Hex_Digit_Display hex_digit_display_7 (.value(system_bus_1_databus));  // open: dp
  Register_4bit register_4bit_4 (
    .in_1(register_4bit_3_out_3), .LD(controlunit_1_output_ld), .out_3(register_4bit_4_out_3));
  Hex_Digit_Display hex_digit_display_8 (.value(register_4bit_4_out_3));  // open: dp
  System_Bus system_bus_1 (
    .IR(ir_1_out_4), .BR(BR_out_3), .CR(register_4bit_1_out_3), .DR(register_4bit_2_out_3),
    .ACC(register_4bit_3_out_3), .MEM(ram_1_dout), .MEM_SELECT(controlunit_1_mem_select),
    .ACC_SELECT(controlunit_1_acc_select), .MOV_Switch(controlunit_1_mov_switch), .L_LD(controlunit_1_al_ld),
    .PC({controlunit_1_out_12_2, controlunit_1_out_12}), .H_LD(controlunit_1_ah_ld),
    .PC_EN(controlunit_1_pc_en), .DataBus(system_bus_1_databus), .REG1(system_bus_1_reg1),
    .REG2(system_bus_1_reg2), .REG3(system_bus_1_reg3), .REG4(system_bus_1_reg4),
    .AddressBus(system_bus_1_addressbus));  // open: ALU_Output, ALU_OP

  // Notes on the sheet:
  //   IR
  //   BR
  //   CR
  //   DR
  //   ACC
  //   Output
endmodule

module PC (
  input  EN,
  input  CLK,
  input  RST,
  input  LD,
  input  D0,
  input  D1,
  input  D2,
  input  D3,
  input  D4,
  input  D5,
  input  D6,
  input  D7,
  output out_13,
  output out_14,
  output out_15,
  output out_16,
  output out_17,
  output out_18,
  output out_19,
  output out_20
);

  wire and_1_out, and_2_out, and_3_out, and_4_out, and_5_out, and_6_out, multiplexer_1_out,
       multiplexer_2_out, multiplexer_3_out, multiplexer_4_out, multiplexer_5_out, multiplexer_6_out,
       multiplexer_7_out, multiplexer_8_out;

  J_K_Flip_Flop j_k_ff_1 (
    .J(multiplexer_1_out), .K(multiplexer_1_out), .clk(CLK), .Q(out_13), .reset(RST));  // open: Qn, preset
  Multiplexer multiplexer_1 (.in0(EN), .in1(D0), .out(multiplexer_1_out), .sel(LD));
  Multiplexer multiplexer_2 (.in0(out_13), .in1(D1), .out(multiplexer_2_out), .sel(LD));
  J_K_Flip_Flop j_k_ff_2 (
    .J(multiplexer_2_out), .K(multiplexer_2_out), .clk(CLK), .Q(out_14), .reset(RST));  // open: Qn, preset
  and and_1 (and_1_out, multiplexer_2_out, out_14);
  Multiplexer multiplexer_3 (.in0(and_1_out), .in1(D2), .out(multiplexer_3_out), .sel(LD));
  J_K_Flip_Flop j_k_ff_3 (
    .J(multiplexer_3_out), .K(multiplexer_3_out), .clk(CLK), .Q(out_15), .reset(RST));  // open: Qn, preset
  and and_2 (and_2_out, out_15, and_1_out);
  J_K_Flip_Flop j_k_ff_4 (
    .J(multiplexer_4_out), .K(multiplexer_4_out), .clk(CLK), .Q(out_16), .reset(RST));  // open: Qn, preset
  Multiplexer multiplexer_4 (.in0(and_2_out), .in1(D3), .out(multiplexer_4_out), .sel(LD));
  and and_3 (and_3_out, out_16, and_2_out);
  J_K_Flip_Flop j_k_ff_5 (
    .J(multiplexer_5_out), .K(multiplexer_5_out), .clk(CLK), .Q(out_17), .reset(RST));  // open: Qn, preset
  Multiplexer multiplexer_5 (.in0(and_3_out), .in1(D4), .out(multiplexer_5_out), .sel(LD));
  and and_4 (and_4_out, multiplexer_5_out, out_17);
  Multiplexer multiplexer_6 (.in0(and_4_out), .in1(D5), .out(multiplexer_6_out), .sel(LD));
  J_K_Flip_Flop j_k_ff_6 (
    .J(multiplexer_6_out), .K(multiplexer_6_out), .clk(CLK), .Q(out_18), .reset(RST));  // open: Qn, preset
  and and_5 (and_5_out, out_18, and_4_out);
  J_K_Flip_Flop j_k_ff_7 (
    .J(multiplexer_7_out), .K(multiplexer_7_out), .clk(CLK), .Q(out_19), .reset(RST));  // open: Qn, preset
  Multiplexer multiplexer_7 (.in0(and_5_out), .in1(D6), .out(multiplexer_7_out), .sel(LD));
  and and_6 (and_6_out, out_19, and_5_out);
  Multiplexer multiplexer_8 (.in0(and_6_out), .in1(D7), .out(multiplexer_8_out), .sel(LD));
  J_K_Flip_Flop j_k_ff_8 (
    .J(multiplexer_8_out), .K(multiplexer_8_out), .clk(CLK), .Q(out_20), .reset(RST));  // open: Qn, preset
endmodule

module SignalGen_Template (
  output [15:0] T,
  output [15:0] OP,
  output out_3
);

  // OR_Gate or_1 has open pins: out=out_3
endmodule

module MEM_READ_SignalGen (
  input  [15:0] T,
  input  [15:0] OP,
  output MEM_READ
);

  wire or_1_out;

  or or_1 (or_1_out, OP[11], OP[2], OP[13]);
  or or_2 (MEM_READ, T[0], T[1], OP[0], OP[1], or_1_out);
endmodule

module PC_EN_SignalGen (
  input  [15:0] T,
  input  [15:0] OP,
  output PC_EN
);

  wire and_1_out, and_2_out, nor_1_out, not_1_out, or_1_out;

  not not_1 (not_1_out, T[5]);
  and and_1 (and_1_out, not_1_out, OP[0]);
  nor nor_1 (nor_1_out, T[0], T[1], T[2], T[8], T[9], T[10]);
  or or_1 (or_1_out, and_1_out, OP[1], OP[2], OP[11], OP[13]);
  and and_2 (and_2_out, nor_1_out, or_1_out);
  or or_2 (PC_EN, T[0], T[1], and_2_out);
endmodule

module MEM_WRITE_SignalGen (
  input  [15:0] T,
  input  [15:0] OP,
  output MEM_WRITE
);

  wire and_1_out;

  and and_1 (and_1_out, T[9], OP[13]);
  buf or_1 (MEM_WRITE, and_1_out);  // OR_Gate
endmodule

module IR_LD_SignalGen (
  input  [15:0] T,
  input  [15:0] OP,
  output IR_LD
);

  buf or_1 (IR_LD, T[2]);  // OR_Gate
endmodule

module AL_LD_SignalGen (
  input  [15:0] T,
  input  [15:0] OP,
  output AL_LD
);

  wire and_1_out, or_1_out;

  or or_1 (or_1_out, OP[0], OP[11], OP[2], OP[13]);
  and and_1 (and_1_out, T[5], or_1_out);
  buf or_2 (AL_LD, and_1_out);  // OR_Gate
endmodule

module AH_LD_SignalGen (
  input  [15:0] T,
  input  [15:0] OP,
  output AH_LD
);

  wire and_1_out, or_1_out;

  or or_1 (or_1_out, OP[11], OP[2], OP[13]);
  and and_1 (and_1_out, T[8], or_1_out);
  buf or_2 (AH_LD, and_1_out);  // OR_Gate
endmodule

module ACC_SELECT_SignalGen (
  input  [15:0] T,
  input  [15:0] OP,
  output ACC_SELECT
);

  wire and_1_out, or_1_out;

  or or_1 (or_1_out, T[9], T[10]);
  and and_1 (and_1_out, or_1_out, OP[13]);
  buf or_2 (ACC_SELECT, and_1_out);  // OR_Gate
endmodule

module ACC_LD_SignalGen (
  input  [15:0] T,
  input  [15:0] OP,
  output ACC_LD
);

  wire and_1_out, and_2_out, and_3_out, or_1_out, or_2_out;

  or or_1 (or_1_out, OP[3], OP[5], OP[8], OP[9], OP[10], OP[12], OP[14], OP[15]);
  or or_2 (or_2_out, OP[11], OP[13]);
  and and_1 (and_1_out, T[3], or_1_out);
  and and_2 (and_2_out, T[5], OP[1]);
  and and_3 (and_3_out, T[10], or_2_out);
  or or_3 (ACC_LD, and_1_out, and_2_out, and_3_out);
endmodule

module MEM_SELECT_SignalGen (
  input  [15:0] T,
  input  [15:0] OP,
  output MEM_SELECT
);

  wire and_1_out, not_1_out;

  not not_1 (not_1_out, T[5]);
  and and_1 (and_1_out, not_1_out, OP[0]);
  or or_1 (MEM_SELECT, OP[1], and_1_out, OP[11]);
endmodule

module PC_CLK_SignalGen (
  input  [15:0] T,
  input  [15:0] OP,
  output PC_CLK
);

  wire and_1_out, and_2_out, or_1_out;

  and and_1 (and_1_out, T[9], OP[2]);
  and and_2 (and_2_out, T[11], or_1_out);
  or or_1 (or_1_out, OP[11], OP[13]);
  or or_2 (PC_CLK, T[2], T[5], and_2_out, and_1_out);
endmodule

module T_RST_SignalGen (
  input  [15:0] T,
  input  [15:0] OP,
  output T_RST
);

  wire and_1_out, and_2_out, and_3_out, and_4_out, and_5_out, and_6_out, or_1_out, or_2_out;

  or or_1 (or_1_out, OP[3], OP[5], OP[8], OP[9], OP[10], OP[12], OP[14], OP[15]);
  and and_1 (and_1_out, T[3], OP[4]);
  and and_2 (and_2_out, T[9], OP[2]);
  and and_3 (and_3_out, T[3], or_1_out);
  and and_4 (and_4_out, T[6], OP[0]);
  and and_5 (and_5_out, T[6], OP[1]);
  and and_6 (and_6_out, T[11], or_2_out);
  or or_2 (or_2_out, OP[11], OP[13]);
  or or_3 (T_RST, and_4_out, and_3_out, and_2_out, and_1_out, and_5_out, and_6_out);
endmodule

module ALU_EN_SignalGen (
  input  [15:0] T,
  input  [15:0] OP,
  output ALU_EN
);

  wire and_1_out, or_1_out, or_2_out, undriven;

  or or_1 (or_1_out, undriven, T[2]);
  or or_2 (or_2_out, OP[3], OP[5], OP[8], OP[9], OP[10], OP[12], OP[14], OP[15]);
  and and_1 (and_1_out, or_1_out, or_2_out);
  buf or_3 (ALU_EN, and_1_out);  // OR_Gate
endmodule

module PC_LD_SignalGen (
  input  [15:0] T,
  input  Z_Flag,
  input  [15:0] OP,
  output PC_LD
);

  wire and_1_out, not_1_out, or_1_out;

  not not_1 (not_1_out, Z_Flag);
  or or_1 (or_1_out, T[8], T[9]);
  and and_1 (and_1_out, or_1_out, not_1_out, OP[2]);
  buf or_2 (PC_LD, and_1_out);  // OR_Gate
endmodule

module FlagsEn_SignalGen (
  input  [15:0] T,
  input  [15:0] OP,
  output ALU_EN
);

  wire and_1_out, or_1_out, or_2_out;

  or or_1 (or_1_out, T[3], T[2]);
  or or_2 (or_2_out, OP[3], OP[5], OP[8], OP[9], OP[10], OP[12], OP[14], OP[15]);
  and and_1 (and_1_out, or_1_out, or_2_out);
  buf or_3 (ALU_EN, and_1_out);  // OR_Gate
endmodule

module IR (
  input  [3:0] in_1,
  input  LD,
  input  RST,
  output [3:0] out_4
);

  wire not_1_out, not_2_out, not_3_out, not_4_out, or_1_out;
  wire [3:0] multiplexer_1_out;

  Multiplexer #(.width(4)) multiplexer_1 (.in0(in_1), .in1(4'b0000), .out(multiplexer_1_out), .sel(RST));
  not not_1 (not_1_out, RST);
  not not_2 (not_2_out, not_1_out);
  not not_3 (not_3_out, not_2_out);
  not not_4 (not_4_out, not_3_out);
  or or_1 (or_1_out, LD, not_4_out);
  PIPO_Register pipo_register_1 (
    .in_1(multiplexer_1_out[0]), .in_2(multiplexer_1_out[1]), .in_3(multiplexer_1_out[2]),
    .in_4(multiplexer_1_out[3]), .LD(or_1_out), .out_6(out_4[0]), .out_7(out_4[1]), .out_8(out_4[2]),
    .out_9(out_4[3]));
endmodule
